# Fritzing sketch skinOS_Zara_v2 (saved by Fritzing 0.9.2b)
breadboards: 1

parts:
  proto1 = Adafruit Feather Wing Proto
  neopixel1 = Neopixel Ring 16
  L1 = Inductor [package="0805 [SMD]"]
  X1 = USB Connectors [package=usb-a-s]
  L2 = Inductor [package="0805 [SMD]"]
  Part1 = Arduino Micro (Rev3)
  R2 = Resistor [tolerance=±5% resistance=330 package="0402 [SMD]"]
  MOTOR1 = Vibration Motor
  MOTOR2 = Vibration Motor
  MOTOR3 = Vibration Motor
  MOTOR4 = Vibration Motor
  R3 = Resistor [tolerance=±5% resistance=1M package="0603 [SMD]"]
  R4 = Resistor [tolerance=±5% resistance=1M package="0603 [SMD]"]

nets:
  N1: proto1.connector92, Part1.D6_PWM/A7
  N2: neopixel1.IN, R2.Pin_0
  N3: L1.pin_0, MOTOR4.NEG
  N4: L1.pin_1, Part1.D2/SDA
  N5: X1.GND, L2.pin_0
  N6: X1.VBUS, L2.pin_1
  N7: Part1.D3/SCL, R2.Pin_1
  N8: Part1.D5_PWM, Part1.D12_PWM/A11, R4.Pin_0, R4.Pin_1
  N9: Part1.D9_PWM/A9, R3.Pin_0, R3.Pin_1
  N10: Part1.D10_PWM/A10, MOTOR1.POS
  N11: MOTOR1.NEG, MOTOR2.POS
  N12: MOTOR2.NEG, MOTOR3.POS
  N13: MOTOR3.NEG, MOTOR4.POS

notes:
  NeoPixel Featherwing
  (attaches on Feather Pin D6)
  Adafruit Feather 32u4 Proto
  (use pin #s shown here)
  clarsonic
  induction coil
  w/ circuit
  CHARGING BASE
  clarsonic
  induction coil
  w/ circuit
  D13^
  Capacitve Touch spots
  (aluminum)

custom parts:
  Neopixel Ring 16: Neopixel Ring x16
  Vibration Motor: An eccentric vibration motor!
